# Fritzing sketch Ldr_with_raspberry (saved by Fritzing 0.9.6b)
breadboards: 1

parts:
  Mod1 = Raspberry Pi 4B
  R1 = Photocell (LDR) [package=THT]
  C1 = Electrolytic Capacitor [capacitance=100μF voltage=35V package="0807 [SMD, electrolytic]"]
  LED1 = LED - 5mm [color="Red (633nm)" current=0.030 package="5 mm [THT]"]
  R2 = Resistor [tolerance=±5% resistance=10000 package="2010 [SMD]"]

nets:
  N1: Mod1.GND, C1.-, LED1.cathode, R2.Pin_1
  N2: Mod1.GPIO23, LED1.anode
  N3: Mod1.GPIO24, R1.pin_0, C1.+, R2.Pin_0
